// Logisim project main_pomysly.circ as structural Verilog: 1 circuit, main circuit main
module main (
  input  in_1,
  input  [23:0] in_2,
  input  [23:0] in_3,
  input  [23:0] in_4,
  input  [23:0] in_5,
  input  [23:0] in_6,
  input  [23:0] in_7,
  input  [23:0] in_8,
  input  [23:0] in_9
);

  wire A, CLK_IN, clock_1_out, D, d_ff_1_q, d_ff_1_qn, Key_impulse, keyboard_1_avail, RESET, Start_Stop,
       TIMEOUT;
  wire [1:0] key;
  wire [2:0] and_2_out, and_3_out, bit_extender_1_out, bit_extender_2_out, Counter;
  wire [3:0] H1, H2, H3, H4;
  wire [6:0] keyboard_1_data, register_1_q;
  wire [23:0] main_4_out_4, main_4_out_5, main_4_out_6, main_4_out_7, main_4_out_8, main_4_out_9,
       main_4_out_10, main_4_out_11, main_5_out_4, main_5_out_5, main_5_out_6, main_5_out_7, main_5_out_8,
       main_5_out_9, main_5_out_10, main_5_out_11, main_6_out_4, main_6_out_5, main_6_out_6, main_6_out_7,
       main_6_out_8, main_6_out_9, main_6_out_10, main_6_out_11, main_7_out_4, main_7_out_5, main_7_out_6,
       main_7_out_7, main_7_out_8, main_7_out_9, main_7_out_10, main_7_out_11, main_8_o1, main_8_o2,
       main_8_o2_2, main_8_o2_3, main_8_o2_4, main_8_o2_5, main_8_o2_6, main_8_o2_7, multiplexer_1_out,
       or_1_out, rom_1_data, rom_2_data, rom_3_data, rom_4_data, rom_5_data;
  wire [31:0] Timer;

  Button button_1 (.out(Start_Stop));
  Button button_2 (.out(RESET));
  DotMatrix #(.matrixcols(32), .matrixrows(1)) dotmatrix_1 (
    .col0(Timer[31]), .col1(Timer[30]), .col2(Timer[29]), .col3(Timer[28]), .col4(Timer[27]),
    .col5(Timer[26]), .col6(Timer[25]), .col7(Timer[24]), .col8(Timer[23]), .col9(Timer[22]),
    .col10(Timer[21]), .col11(Timer[20]), .col12(Timer[19]), .col13(Timer[18]), .col14(Timer[17]),
    .col15(Timer[16]), .col16(Timer[15]), .col17(Timer[14]), .col18(Timer[13]), .col19(Timer[12]),
    .col20(Timer[11]), .col21(Timer[10]), .col22(Timer[9]), .col23(Timer[8]), .col24(Timer[7]),
    .col25(Timer[6]), .col26(Timer[5]), .col27(Timer[4]), .col28(Timer[3]), .col29(Timer[2]),
    .col30(Timer[1]), .col31(Timer[0]));
  Clock clock_1 (.out(clock_1_out));
  D_Flip_Flop d_ff_1 (.clk(Start_Stop), .D(d_ff_1_qn), .Q(d_ff_1_q), .Qn(d_ff_1_qn));  // open: preset, en, reset
  Hex_Digit_Display hex_digit_display_1 (.value(H4));  // open: dp
  and and_1 (CLK_IN, clock_1_out, d_ff_1_q);
  Hex_Digit_Display hex_digit_display_2 (.value(H3));  // open: dp
  Hex_Digit_Display hex_digit_display_3 (.value(H2));  // open: dp
  PointCounter_main main_1 (.ADD(CLK_IN), .RESET(RESET), .X000(H4), ._0X00(H3), ._00X0(H2), ._000X(H1));  // open: LIMIT
  TIMEDISPLAY_main main_2 (
    .WHEN_1__SUB_TIME_ONE_TICK__WHEN_0_ADD_TIME_ON_TICK(in_1), .CLK(CLK_IN), .RESET(RESET),
    .OutputScreen(Timer), .TIME_OUT(TIMEOUT));
  Hex_Digit_Display hex_digit_display_4 (.value(H1));  // open: dp
  Stop_countera_main main_3 (.Clk(CLK_IN), .Reset(Key_impulse), .Counter(Counter));
  assign bit_extender_1_out = {{2{D}}, D};  // Bit_Extender bit_extender_1
  assign bit_extender_2_out = {{2{A}}, A};  // Bit_Extender bit_extender_2
  ROM #(.addrWidth(3), .dataWidth(24)) rom_1 (.addr(Counter), .data(rom_1_data));  // open: sel
  ROM #(.addrWidth(3), .dataWidth(24)) rom_2 (.addr(Counter), .data(rom_2_data));  // open: sel
  ROM #(.addrWidth(3), .dataWidth(24)) rom_3 (.addr(Counter), .data(rom_3_data));  // open: sel
  assign and_2_out = Counter & bit_extender_1_out;  // AND_Gate and_2, 3 bits wide
  assign and_3_out = Counter & bit_extender_2_out;  // AND_Gate and_3, 3 bits wide
  ROM #(.addrWidth(3), .dataWidth(24)) rom_4 (.addr(and_2_out), .data(rom_4_data));  // open: sel
  ROM #(.addrWidth(3), .dataWidth(24)) rom_5 (.addr(and_3_out), .data(rom_5_data));  // open: sel
  Multiplexer #(.select(2), .width(24)) multiplexer_1 (
    .in1(rom_4_data), .in2(rom_5_data), .out(multiplexer_1_out), .sel(key));  // open: in0, in3, en
  assign or_1_out = rom_3_data | multiplexer_1_out;  // OR_Gate or_1, 24 bits wide
  Display_segment_control_main main_4 (
    .ROM_in(rom_2_data), .Clk(CLK_IN), .out_4(main_4_out_4), .out_5(main_4_out_5), .out_6(main_4_out_6),
    .out_7(main_4_out_7), .out_8(main_4_out_8), .out_9(main_4_out_9), .out_10(main_4_out_10),
    .out_11(main_4_out_11));  // open: Reset
  DotMatrix #(.inputtype("row"), .matrixcols(24), .matrixrows(8)) dotmatrix_2 (
    .row0(main_4_out_4), .row1(main_4_out_5), .row2(main_4_out_6), .row3(main_4_out_7), .row4(main_4_out_8),
    .row5(main_4_out_9), .row6(main_4_out_10), .row7(main_4_out_11));
  Display_segment_control_main main_5 (
    .ROM_in(rom_1_data), .Clk(CLK_IN), .out_4(main_5_out_4), .out_5(main_5_out_5), .out_6(main_5_out_6),
    .out_7(main_5_out_7), .out_8(main_5_out_8), .out_9(main_5_out_9), .out_10(main_5_out_10),
    .out_11(main_5_out_11));  // open: Reset
  DotMatrix #(.inputtype("row"), .matrixcols(24), .matrixrows(8)) dotmatrix_3 (
    .row0(main_5_out_4), .row1(main_5_out_5), .row2(main_5_out_6), .row3(main_5_out_7), .row4(main_5_out_8),
    .row5(main_5_out_9), .row6(main_5_out_10), .row7(main_5_out_11));
  DotMatrix #(.inputtype("row"), .matrixcols(24), .matrixrows(8)) dotmatrix_4 (
    .row0(main_6_out_4), .row1(main_6_out_5), .row2(main_6_out_6), .row3(main_6_out_7), .row4(main_6_out_8),
    .row5(main_6_out_9), .row6(main_6_out_10), .row7(main_6_out_11));
  Display_segment_control_main main_6 (
    .ROM_in(rom_3_data), .Clk(CLK_IN), .out_4(main_6_out_4), .out_5(main_6_out_5), .out_6(main_6_out_6),
    .out_7(main_6_out_7), .out_8(main_6_out_8), .out_9(main_6_out_9), .out_10(main_6_out_10),
    .out_11(main_6_out_11));  // open: Reset
  Display_segment_control_main main_7 (
    .ROM_in(rom_3_data), .Clk(CLK_IN), .out_4(main_7_out_4), .out_5(main_7_out_5), .out_6(main_7_out_6),
    .out_7(main_7_out_7), .out_8(main_7_out_8), .out_9(main_7_out_9), .out_10(main_7_out_10),
    .out_11(main_7_out_11));  // open: Reset
  DotMatrix #(.inputtype("row"), .matrixcols(24), .matrixrows(8)) dotmatrix_5 (
    .row0(main_7_out_4), .row1(main_7_out_5), .row2(main_7_out_6), .row3(main_7_out_7), .row4(main_7_out_8),
    .row5(main_7_out_9), .row6(main_7_out_10), .row7(main_7_out_11));
  DotMatrix #(.inputtype("row"), .matrixcols(24), .matrixrows(8)) dotmatrix_6 (
    .row0(main_8_o1), .row1(main_8_o2), .row2(main_8_o2_2), .row3(main_8_o2_3), .row4(main_8_o2_4),
    .row5(main_8_o2_5), .row6(main_8_o2_6), .row7(main_8_o2_7));
  Display_first_segment_control_main main_8 (
    .In(or_1_out), .Clk(CLK_IN), .Counter(Counter), .O1(main_8_o1), .O2(main_8_o2), .O2_2(main_8_o2_2),
    .O2_3(main_8_o2_3), .O2_4(main_8_o2_4), .O2_5(main_8_o2_5), .O2_6(main_8_o2_6), .O2_7(main_8_o2_7));  // open: Reset
  Pull_Resistor pull_resistor_1 (.node(Key_impulse));
  Keyboard keyboard_1 (.clk(Key_impulse), .re(1'b1), .avail(keyboard_1_avail), .data(keyboard_1_data));  // open: clr
  assign Key_impulse = keyboard_1_avail ? CLK_IN : 1'bz;  // Controlled_Buffer controlled_buffer_1
  // Probe on in_2
  // Probe on in_3
  // Probe on in_4
  // Probe on in_7
  DotMatrix #(.inputtype("row"), .matrixcols(24), .matrixrows(8)) dotmatrix_7 (
    .row0(in_2), .row1(in_3), .row2(in_4), .row3(in_7), .row4(in_5), .row5(in_8), .row6(in_6), .row7(in_9));
  Register #(.width(7)) register_1 (.D(keyboard_1_data), .Q(register_1_q), .clk(Key_impulse));  // open: en, clr
  // Probe on in_5
  // Probe on in_8
  Key_recognition_main main_9 (.Keyboard_input(register_1_q), .Out(key), .Clk(CLK_IN), .A(A), .D(D));
  // Probe on in_6
  // Probe on in_9

  // Other names for the same wires on the sheet: _1[23:0] = in_2; _2[23:0] = in_3; _3[23:0] = in_4; _4[23:0] = in_7;
  //   _5[23:0] = in_5; _6[23:0] = in_8; _7[23:0] = in_6; _8[23:0] = in_9

  // Notes on the sheet:
  //   contents of rom_1 (hex, n*v repeats v):
  //   7e00 7e08 7f1c 7ffe 7f9c 7e08 7e00 7e00
  //   contents of rom_2 (hex, n*v repeats v):
  //   7e00 10fe00 38fe00 7ffe00 39fe00 107e00 7e00 7e00
  //   contents of rom_3 (hex, n*v repeats v):
  //   8*7e00
  //   contents of rom_4 (hex, n*v repeats v):
  //   0 c cc de 7e 4e c 33
  //   contents of rom_5 (hex, n*v repeats v):
  //   0 300000 330000 7b0000 7e0000 720000 300000 cc0000
endmodule
